# Fritzing sketch mircoffee (saved by Fritzing 0.9.3b)
breadboards: 1

parts:
  DS1 = DS18B20 1-Wire Temperature Sensor [part_number=DS18B20]
  Part1 = Arduino Uno (Rev3)
  R1 = Resistor [tolerance=±5% resistance=4.7k package=THT]
  U1 = 2-Channel 5v Relay Shield [package=relay-2ch5v10a]
  Part2 = DeuLigne 1.1 - The Snootlab's LCD shield for Arduino  # not connected

nets:
  GND: DS1.GND, Part1.GND, U1.GND
  N1: DS1.DQ, Part1.D2, R1.Pin_1
  VDD: DS1.VDD, Part1.5V, R1.Pin_0, U1.VCC
  N2: Part1.A4/SDA, U1.IN1

custom parts:
  2-Channel 5v Relay Shield: 2 Channel 5v Relay Shield w. 2x SPD-06VDC-SD-C
